// Logisim project BCD_Adder.circ as structural Verilog: 1 circuit, main circuit main
module main (
  input  [3:0] in_1,
  input  [3:0] in_2,
  input  in_3
);

  wire adder_1_cout, and_1_out, and_2_out;
  wire [2:2] or_1_out;
  wire [3:0] adder_1_out, adder_2_out;

  Adder #(.width(4)) adder_1 (.a(in_1), .b(in_2), .out(adder_1_out), .cout(adder_1_cout));  // open: cin
  and and_1 (and_1_out, adder_1_out[3], adder_1_out[2]);
  and and_2 (and_2_out, adder_1_out[3], adder_1_out[1]);
  or or_1 (or_1_out[2], and_1_out, adder_1_cout, and_2_out);
  Adder #(.width(4)) adder_2 (
    .a(adder_1_out), .b({in_3, {2{or_1_out[2]}}, in_3}), .out(adder_2_out));  // open: cin, cout
  LedBar #(.matrixcols(5)) ledbar_1 (
    .led0(or_1_out[2]), .led1(adder_2_out[3]), .led2(adder_2_out[2]), .led3(adder_2_out[1]),
    .led4(adder_2_out[0]));
endmodule
