// Logisim project Decoder3X8.circ as structural Verilog: 1 circuit, main circuit main
module main (
  input  X,
  input  in_2,
  input  Z
);

  wire and_1_out, and_2_out, and_3_out, and_4_out, and_5_out, and_6_out, and_7_out, and_8_out, and_9_out,
       and_10_out, and_11_out, and_12_out, and_13_out, and_14_out, and_15_out, and_16_out, not_1_out,
       not_2_out, not_3_out;

  not not_1 (not_1_out, X);
  not not_2 (not_2_out, in_2);
  not not_3 (not_3_out, Z);
  and and_1 (and_1_out, not_1_out, not_2_out);
  and and_2 (and_2_out, X, in_2);
  and and_3 (and_3_out, X, not_2_out);
  and and_4 (and_4_out, not_1_out, not_2_out);
  and and_5 (and_5_out, not_1_out, in_2);
  and and_6 (and_6_out, not_1_out, in_2);
  and and_7 (and_7_out, X, in_2);
  and and_8 (and_8_out, X, not_2_out);
  and and_9 (and_9_out, and_1_out, not_3_out);
  and and_10 (and_10_out, and_2_out, Z);
  and and_11 (and_11_out, and_3_out, not_3_out);
  and and_12 (and_12_out, and_4_out, Z);
  and and_13 (and_13_out, and_5_out, not_3_out);
  and and_14 (and_14_out, and_6_out, Z);
  and and_15 (and_15_out, and_7_out, not_3_out);
  and and_16 (and_16_out, and_8_out, Z);

  // Notes on the sheet:
  //   X'
  //   Y
  //   Y'
  //   Z'
  //   X'Y'Z'
  //   XYZ
  //   XY'Z'
  //   X'Y'Z
  //   X'YZ'
  //   X'YZ
  //   XYZ'
  //   XY'Z
endmodule
