// Logisim project Dflipflopp.circ as structural Verilog: 2 circuits, main circuit main
module main (
  input  in_1,
  output out_2,
  output out_3
);

  wire clock_1_out, nand_1_out, nand_2_out, not_1_out;

  Clock clock_1 (.out(clock_1_out));
  not not_1 (not_1_out, in_1);
  nand nand_1 (nand_1_out, in_1, clock_1_out);
  nand nand_2 (nand_2_out, clock_1_out, not_1_out);
  nand nand_3 (out_2, nand_1_out, out_3);
  nand nand_4 (out_3, out_2, nand_2_out);
endmodule

module Dflipflop (
  input  in_1,
  output out_2,
  output out_3
);

  wire clock_1_out;

  Clock clock_1 (.out(clock_1_out));
  main main_1 (.in_1(in_1), .out_2(out_2), .out_3(out_3));
endmodule
