// Logisim project Encoder.circ as structural Verilog: 1 circuit, main circuit main
module main (
  input  in_1,
  input  in_2,
  input  in_3,
  input  in_4,
  input  in_5,
  input  in_6
);

  wire clock_1_out, nand_1_out, nand_4_out, not_1_out;

  not not_1 (not_1_out, in_2);
  Clock clock_1 (.out(clock_1_out));
  nand nand_1 (nand_1_out, in_2, clock_1_out);
  nand nand_2 (in_1, clock_1_out, not_1_out);
  D_Flip_Flop d_ff_1 (.D(in_4), .clk(in_5), .Q(in_3), .Qn(in_6));  // open: preset, reset
  nand nand_3 (in_1, nand_1_out, nand_4_out);
  not nand_4 (nand_4_out, in_1);  // NAND_Gate
  LED led_1 (.in(in_1));
  LED led_2 (.in(nand_4_out));
endmodule
