// Logisim project LookAheadCarry.circ as structural Verilog: 1 circuit, main circuit main
module main (
  input  in_1,
  input  in_2,
  input  in_3,
  input  in_4,
  input  in_5,
  input  in_6,
  input  C1
);

  wire and_1_out, and_2_out, and_3_out, and_4_out, and_5_out, and_6_out, and_7_out, and_8_out, and_9_out,
       and_10_out, and_11_out, and_12_out, and_13_out, or_1_out, or_2_out, or_3_out, or_4_out, or_5_out,
       or_6_out, xor_1_out, xor_2_out, xor_3_out;

  xor xor_1 (xor_1_out, in_1, in_2);
  and and_1 (and_1_out, in_1, in_2);
  xor xor_2 (xor_2_out, in_3, in_4);
  and and_2 (and_2_out, in_3, in_4);
  xor xor_3 (xor_3_out, in_5, in_6);
  and and_3 (and_3_out, in_5, in_6);
  and and_4 (and_4_out, C1, and_1_out);
  or or_1 (or_1_out, xor_1_out, and_4_out);
  and and_5 (and_5_out, and_2_out, xor_1_out);
  and and_6 (and_6_out, and_1_out, and_2_out);
  and and_7 (and_7_out, xor_2_out, and_3_out);
  and and_8 (and_8_out, and_6_out, C1);
  or or_2 (or_2_out, and_5_out, xor_2_out);
  and and_9 (and_9_out, and_3_out, and_2_out);
  and and_10 (and_10_out, and_2_out, and_3_out);
  and and_11 (and_11_out, and_1_out, C1);
  or or_3 (or_3_out, or_2_out, and_8_out);
  and and_12 (and_12_out, and_9_out, xor_1_out);
  LED led_1 (.in(or_1_out));
  and and_13 (and_13_out, and_10_out, and_11_out);
  LED led_2 (.in(or_3_out));
  or or_4 (or_4_out, and_12_out, and_13_out);
  or or_5 (or_5_out, and_7_out, xor_3_out);
  or or_6 (or_6_out, or_4_out, or_5_out);
  LED led_3 (.in(or_6_out));

  // Notes on the sheet:
  //   P1
  //   G1
  //   P2
  //   G2
  //   P3
  //   G3
  //   C2
  //   C3
  //   C4
endmodule
