// Logisim project MUX_DEMUX.circ as structural Verilog: 1 circuit, main circuit main
module main (
  input  A,
  input  B,
  input  C,
  input  D,
  input  [1:0] s1
);

  wire demultiplexer_1_out0, demultiplexer_1_out1, demultiplexer_1_out2, demultiplexer_1_out3,
       multiplexer_1_out;

  Multiplexer #(.select(2)) multiplexer_1 (.in0(A), .in1(B), .in2(C), .in3(D), .out(multiplexer_1_out), .sel(s1));
  Demultiplexer #(.select(2)) demultiplexer_1 (
    .out0(demultiplexer_1_out0), .out1(demultiplexer_1_out1), .out2(demultiplexer_1_out2),
    .out3(demultiplexer_1_out3), .in(multiplexer_1_out), .sel(s1));
  LED led_1 (.in(demultiplexer_1_out0));
  LED led_2 (.in(demultiplexer_1_out2));
  LED led_3 (.in(demultiplexer_1_out3));
  LED led_4 (.in(demultiplexer_1_out1));

  // Notes on the sheet:
  //   s0
  //   00
  //   01
  //   10
  //   11
endmodule
