// Logisim project SR_FlipFlop.circ as structural Verilog: 1 circuit, main circuit main
module main (
);

  wire clock_1_out, s_r_ff_1_q, s_r_ff_1_qn, undriven, undriven_2;

  Clock clock_1 (.out(clock_1_out));
  S_R_Flip_Flop s_r_ff_1 (
    .S(undriven_2), .R(undriven), .clk(clock_1_out), .Q(s_r_ff_1_q), .Qn(s_r_ff_1_qn));  // open: reset, preset
  D_Flip_Flop d_ff_1 ();  // open: D, clk, Q, Qn, preset, reset
  LED led_1 (.in(s_r_ff_1_q));
  LED led_2 (.in(s_r_ff_1_qn));
endmodule
