// Logisim project adder_all.circ as structural Verilog: 1 circuit, main circuit main
module main (
  input  x,
  input  y,
  input  in_3,
  input  in_4,
  input  z,
  input  x_2,
  input  y_2,
  input  in_8,
  input  in_9,
  input  z_2
);

  wire and_1_out, and_2_out, and_3_out, and_4_out, and_5_out, and_6_out, and_7_out, and_8_out, not_1_out,
       not_2_out, not_3_out, or_1_out, or_2_out, xor_1_out, xor_2_out, xor_3_out, xor_4_out, xor_5_out,
       xor_6_out;

  and and_1 (and_1_out, x, y);
  and and_2 (and_2_out, in_3, in_4);
  xor xor_1 (xor_1_out, x, y);
  LED led_1 (.in(and_1_out));
  xor xor_2 (xor_2_out, in_3, in_4);
  and and_3 (and_3_out, in_3, z);
  not not_1 (not_1_out, x_2);
  xor xor_3 (xor_3_out, in_8, in_9);
  LED led_2 (.in(xor_1_out));
  and and_4 (and_4_out, in_4, z);
  and and_5 (and_5_out, not_1_out, y_2);
  not not_2 (not_2_out, in_8);
  not not_3 (not_3_out, in_8);
  xor xor_4 (xor_4_out, x_2, y_2);
  LED led_3 (.in(and_5_out));
  and and_6 (and_6_out, not_2_out, z_2);
  and and_7 (and_7_out, in_9, z_2);
  and and_8 (and_8_out, not_3_out, in_9);
  LED led_4 (.in(xor_4_out));
  xor xor_5 (xor_5_out, xor_2_out, z);
  xor xor_6 (xor_6_out, xor_3_out, z_2);
  LED led_5 (.in(xor_5_out));
  LED led_6 (.in(xor_6_out));
  or or_1 (or_1_out, and_4_out, and_2_out, and_3_out);
  LED led_7 (.in(or_1_out));
  or or_2 (or_2_out, and_6_out, and_7_out, and_8_out);
  LED led_8 (.in(or_2_out));

  // Notes on the sheet:
  //   x
  //   y
  //   x
  //   y
  //   half adder
  //   c
  //   full adder
  //   half subtractor
  //   full subtractor
  //   s
  //   B
  //   a
  //   D
  //   truth table
  //   b
  //   s
  //   0    0
  //   0     1
  //   1     0
  //   1     1
  //   c
  //   s
  //   D
  //   c
  //   B
endmodule
