// Logisim project counter_all.circ as structural Verilog: 1 circuit, main circuit main
module main (
  input  \logic ,
  input  reset,
  input  logic_2,
  input  reset_2,
  input  logic_3,
  input  in_6,
  input  logic_4,
  input  in_8,
  output msb,
  output out_10,
  output out_11,
  output LSB,
  output msb_2,
  output out_14,
  output out_15,
  output LSB_2,
  output out_17,
  output out_18,
  output out_19,
  output out_20,
  output out_21,
  output out_22,
  output out_23,
  output out_24
);

  wire clock_1_out, clock_2_out, clock_3_out, clock_4_out, clock_5_out, d_ff_1_q, d_ff_2_q, d_ff_3_q,
       d_ff_4_qn, j_k_ff_2_qn, j_k_ff_4_qn, j_k_ff_6_qn, not_1_out, not_2_out, not_3_out, not_4_out,
       not_5_out, not_6_out, not_7_out, not_8_out, not_9_out, not_10_out, not_11_out, not_12_out, not_13_out,
       not_14_out, not_15_out, not_16_out, t_ff_2_q, t_ff_4_q, t_ff_6_q;

  Clock clock_1 (.out(clock_1_out));
  J_K_Flip_Flop j_k_ff_1 (.J(\logic ), .K(\logic ), .clk(not_1_out), .Q(LSB), .reset(reset));  // open: Qn, preset
  not not_1 (not_1_out, clock_1_out);
  Clock clock_2 (.out(clock_2_out));
  not not_2 (not_2_out, clock_2_out);
  Clock clock_3 (.out(clock_3_out));
  Clock clock_4 (.out(clock_4_out));
  Clock clock_5 (.out(clock_5_out));
  J_K_Flip_Flop j_k_ff_2 (
    .J(logic_2), .K(logic_2), .clk(not_2_out), .Q(LSB_2), .Qn(j_k_ff_2_qn), .reset(reset_2));  // open: preset
  T_Flip_Flop t_ff_1 (.T(logic_3), .clk(not_3_out), .Q(out_20), .reset(in_6));  // open: Qn, preset
  not not_3 (not_3_out, clock_3_out);
  T_Flip_Flop t_ff_2 (.T(logic_4), .clk(not_4_out), .Q(t_ff_2_q), .Qn(out_24), .reset(in_8));  // open: preset
  not not_4 (not_4_out, clock_4_out);
  D_Flip_Flop d_ff_1 (.D(d_ff_4_qn), .clk(clock_5_out), .Q(d_ff_1_q));  // open: Qn, preset, reset
  J_K_Flip_Flop j_k_ff_3 (.J(\logic ), .K(\logic ), .clk(not_5_out), .Q(out_11), .reset(reset));  // open: Qn, preset
  not not_5 (not_5_out, LSB);
  T_Flip_Flop t_ff_3 (.T(logic_3), .clk(not_6_out), .Q(out_19), .reset(in_6));  // open: Qn, preset
  not not_6 (not_6_out, out_20);
  T_Flip_Flop t_ff_4 (.T(logic_4), .clk(not_7_out), .Q(t_ff_4_q), .Qn(out_23), .reset(in_8));  // open: preset
  not not_7 (not_7_out, t_ff_2_q);
  J_K_Flip_Flop j_k_ff_4 (
    .J(logic_2), .K(logic_2), .clk(not_8_out), .Q(out_15), .Qn(j_k_ff_4_qn), .reset(reset_2));  // open: preset
  not not_8 (not_8_out, j_k_ff_2_qn);
  D_Flip_Flop d_ff_2 (.D(d_ff_1_q), .clk(clock_5_out), .Q(d_ff_2_q));  // open: Qn, preset, reset
  not not_9 (not_9_out, out_11);
  T_Flip_Flop t_ff_5 (.T(logic_3), .clk(not_10_out), .Q(out_18), .reset(in_6));  // open: Qn, preset
  not not_10 (not_10_out, out_19);
  T_Flip_Flop t_ff_6 (.T(logic_4), .clk(not_11_out), .Q(t_ff_6_q), .Qn(out_22), .reset(in_8));  // open: preset
  not not_11 (not_11_out, t_ff_4_q);
  J_K_Flip_Flop j_k_ff_5 (.J(\logic ), .K(\logic ), .clk(not_9_out), .Q(out_10), .reset(reset));  // open: Qn, preset
  J_K_Flip_Flop j_k_ff_6 (
    .J(logic_2), .K(logic_2), .clk(not_12_out), .Q(out_14), .Qn(j_k_ff_6_qn), .reset(reset_2));  // open: preset
  not not_12 (not_12_out, j_k_ff_4_qn);
  D_Flip_Flop d_ff_3 (.D(d_ff_2_q), .clk(clock_5_out), .Q(d_ff_3_q));  // open: Qn, preset, reset
  T_Flip_Flop t_ff_7 (.T(logic_3), .clk(not_13_out), .Q(out_17), .reset(in_6));  // open: Qn, preset
  not not_13 (not_13_out, out_18);
  T_Flip_Flop t_ff_8 (.T(logic_4), .clk(not_14_out), .Qn(out_21), .reset(in_8));  // open: Q, preset
  not not_14 (not_14_out, t_ff_6_q);
  J_K_Flip_Flop j_k_ff_7 (.J(\logic ), .K(\logic ), .clk(not_15_out), .Q(msb), .reset(reset));  // open: Qn, preset
  not not_15 (not_15_out, out_10);
  D_Flip_Flop d_ff_4 (.D(d_ff_3_q), .clk(clock_5_out), .Qn(d_ff_4_qn));  // open: Q, preset, reset
  J_K_Flip_Flop j_k_ff_8 (.J(logic_2), .K(logic_2), .clk(not_16_out), .Q(msb_2), .reset(reset_2));  // open: Qn, preset
  not not_16 (not_16_out, j_k_ff_6_qn);

  // Notes on the sheet:
  //   clk
  //   clk
  //   reset
  //   clk
  //   clk
  //   1. 4-bit Asynchronous Up counter JK flip-flop
  //   4-bit asynchronous down counter JK Flip Flop
  //   4-bit asynchronous Up counter T Flip Flop
  //   4-bit asynchronous Down counter T Flip Flop
  //   johnson counter synchronous
endmodule
