// Logisim project counter_asy_syn.circ as structural Verilog: 1 circuit, main circuit main
module main (
);

  wire clock_1_out, clock_2_out, d_ff_1_q, d_ff_1_qn, d_ff_2_q, d_ff_2_qn, d_ff_3_q, d_ff_3_qn, d_ff_4_q,
       d_ff_4_qn, d_ff_5_q, d_ff_5_qn, d_ff_6_q, d_ff_6_qn, d_ff_7_q, d_ff_7_qn, d_ff_8_q, d_ff_8_qn;

  Clock clock_1 (.out(clock_1_out));
  Clock clock_2 (.out(clock_2_out));
  D_Flip_Flop d_ff_1 (.D(d_ff_1_qn), .clk(clock_1_out), .Q(d_ff_1_q), .Qn(d_ff_1_qn));  // open: preset, reset
  D_Flip_Flop d_ff_2 (.D(d_ff_2_qn), .clk(clock_2_out), .Q(d_ff_2_q), .Qn(d_ff_2_qn));  // open: preset, reset
  D_Flip_Flop d_ff_3 (.D(d_ff_3_qn), .clk(d_ff_1_qn), .Q(d_ff_3_q), .Qn(d_ff_3_qn));  // open: preset, reset
  D_Flip_Flop d_ff_4 (.D(d_ff_4_qn), .clk(d_ff_2_q), .Q(d_ff_4_q), .Qn(d_ff_4_qn));  // open: preset, reset
  D_Flip_Flop d_ff_5 (.D(d_ff_5_qn), .clk(d_ff_3_qn), .Q(d_ff_5_q), .Qn(d_ff_5_qn));  // open: preset, reset
  D_Flip_Flop d_ff_6 (.D(d_ff_6_qn), .clk(d_ff_4_q), .Q(d_ff_6_q), .Qn(d_ff_6_qn));  // open: preset, reset
  D_Flip_Flop d_ff_7 (.D(d_ff_7_qn), .clk(d_ff_5_qn), .Q(d_ff_7_q), .Qn(d_ff_7_qn));  // open: preset, reset
  D_Flip_Flop d_ff_8 (.D(d_ff_8_qn), .clk(d_ff_6_q), .Q(d_ff_8_q), .Qn(d_ff_8_qn));  // open: preset, reset
  LedBar #(.matrixcols(4)) ledbar_1 (.led0(d_ff_1_q), .led1(d_ff_3_q), .led2(d_ff_5_q), .led3(d_ff_7_q));
  LedBar #(.matrixcols(4)) ledbar_2 (.led0(d_ff_2_q), .led1(d_ff_4_q), .led2(d_ff_6_q), .led3(d_ff_8_q));
endmodule
