// Logisim project multiplexers.circ as structural Verilog: 1 circuit, main circuit main
module main (
  input  in_1,
  input  in_2,
  input  [2:0] in_3,
  input  in_4,
  input  [2:0] in_5
);

  wire demultiplexer_1_out0, demultiplexer_1_out2, demultiplexer_1_out3, demultiplexer_1_out7,
       multiplexer_1_out, not_1_out;

  not not_1 (not_1_out, in_4);
  Multiplexer #(.select(3)) multiplexer_1 (
    .in0(in_1), .in1(in_1), .in2(in_2), .in3(not_1_out), .in4(not_1_out), .in5(in_2), .in6(in_2), .in7(in_4),
    .out(multiplexer_1_out), .sel(in_5));
  LED led_1 (.in(demultiplexer_1_out0));
  Demultiplexer #(.select(3)) demultiplexer_1 (
    .out0(demultiplexer_1_out0), .out1(demultiplexer_1_out0), .out2(demultiplexer_1_out2),
    .out3(demultiplexer_1_out3), .out4(demultiplexer_1_out3), .out5(demultiplexer_1_out2),
    .out6(demultiplexer_1_out2), .out7(demultiplexer_1_out7), .in(multiplexer_1_out), .sel(in_3));
  LED led_2 (.in(demultiplexer_1_out2));
  LED led_3 (.in(demultiplexer_1_out7));
  LED led_4 (.in(demultiplexer_1_out3));
endmodule
