// Logisim project mux_demux_nx.circ as structural Verilog: 1 circuit, main circuit main
module main (
  input  in_1,
  input  in_2,
  input  in_3,
  input  in_4,
  input  in_5,
  input  in_6
);

  wire and_1_out, and_2_out, and_3_out, and_4_out, and_5_out, and_6_out, and_7_out, and_8_out, not_1_out,
       not_2_out, not_3_out, or_1_out;

  not not_1 (not_1_out, in_5);
  not not_2 (not_2_out, in_6);
  and and_1 (and_1_out, in_1, not_1_out, not_2_out);
  and and_2 (and_2_out, in_2, in_5, not_2_out);
  and and_3 (and_3_out, in_3, not_1_out, in_6);
  and and_4 (and_4_out, in_4, in_5, in_6);
  or or_1 (or_1_out, and_1_out, and_2_out, and_3_out, and_4_out);
  not not_3 (not_3_out, or_1_out);
  and and_5 (and_5_out, not_3_out, not_1_out, not_2_out);
  and and_6 (and_6_out, not_3_out, in_5, not_2_out);
  and and_7 (and_7_out, not_3_out, not_1_out, in_6);
  and and_8 (and_8_out, not_3_out, in_5, in_6);
  LED led_1 (.in(and_5_out));
  LED led_2 (.in(and_7_out));
  LED led_3 (.in(and_6_out));
  LED led_4 (.in(and_8_out));
endmodule
