// Logisim project oneboard_mux_demux.circ as structural Verilog: 1 circuit, main circuit main
module main (
  input  S0,
  input  S1,
  input  Io,
  input  I1,
  input  I2,
  input  I3
);

  wire and_1_out, and_2_out, and_3_out, and_4_out, and_5_out, and_6_out, and_7_out, and_8_out, not_1_out,
       not_2_out, not_3_out, or_1_out;

  not not_1 (not_1_out, S0);
  not not_2 (not_2_out, S1);
  and and_1 (and_1_out, Io, not_1_out, not_2_out);
  and and_2 (and_2_out, I1, S0, not_2_out);
  and and_3 (and_3_out, I2, not_1_out, S1);
  and and_4 (and_4_out, I3, S0, S1);
  or or_1 (or_1_out, and_1_out, and_2_out, and_3_out, and_4_out);
  not not_3 (not_3_out, or_1_out);
  and and_5 (and_5_out, not_1_out, not_2_out, not_3_out);
  and and_6 (and_6_out, not_2_out, S0, not_3_out);
  and and_7 (and_7_out, not_1_out, S1, not_3_out);
  and and_8 (and_8_out, S1, S0, not_3_out);
  LED led_1 (.in(and_6_out));
  LED led_2 (.in(and_7_out));
  LED led_3 (.in(and_8_out));
  LED led_4 (.in(and_5_out));

  // Notes on the sheet:
  //   s0
  //   s0 bar
  //   s1
  //   s1 bar
endmodule
