// Logisim project register_all.circ as structural Verilog: 1 circuit, main circuit main
module main (
  input  in_1,
  input  in_2,
  input  in_3,
  input  in_4,
  input  in_5,
  input  in_6,
  input  in_7,
  input  in_8,
  input  in_9,
  input  in_10,
  output out_11,
  output out_12,
  output out_13,
  output out_14,
  output out_15,
  output out_16,
  output out_17,
  output out_18
);

  wire and_1_out, and_2_out, and_3_out, and_4_out, and_5_out, and_6_out, and_7_out, and_8_out, and_9_out,
       and_10_out, and_11_out, and_12_out, and_13_out, and_14_out, and_15_out, and_16_out, button_1_out,
       button_2_out, clock_1_out, clock_2_out, not_1_out, not_2_out, or_1_out, or_2_out, or_3_out, or_4_out,
       or_5_out, or_6_out, or_7_out, or_8_out;

  not not_1 (not_1_out, in_5);
  Clock clock_1 (.out(clock_1_out));
  Button button_1 (.out(button_1_out));
  not not_2 (not_2_out, in_10);
  Clock clock_2 (.out(clock_2_out));
  Button button_2 (.out(button_2_out));
  and and_1 (and_1_out, in_1, in_5);
  or or_1 (or_1_out, and_1_out, and_3_out);
  buf and_2 (and_2_out, in_10);  // AND_Gate
  and and_3 (and_3_out, not_1_out, out_14);
  D_Flip_Flop d_ff_1 (.D(or_1_out), .clk(clock_1_out), .Q(out_14), .reset(button_1_out));  // open: Qn, preset
  buf and_4 (and_4_out, not_2_out);  // AND_Gate
  or or_2 (or_2_out, and_2_out, and_4_out);
  and and_5 (and_5_out, in_2, in_5);
  D_Flip_Flop d_ff_2 (.D(or_2_out), .clk(clock_2_out), .reset(button_2_out));  // open: Q, Qn, preset
  and and_6 (and_6_out, not_1_out, out_12);
  or or_3 (or_3_out, and_5_out, and_6_out);
  buf and_7 (and_7_out, in_10);  // AND_Gate
  or or_4 (or_4_out, and_7_out, and_8_out);
  D_Flip_Flop d_ff_3 (.D(or_3_out), .clk(clock_1_out), .Q(out_12), .reset(button_1_out));  // open: Qn, preset
  buf and_8 (and_8_out, not_2_out);  // AND_Gate
  D_Flip_Flop d_ff_4 (.D(or_4_out), .clk(clock_2_out), .reset(button_2_out));  // open: Q, Qn, preset
  and and_9 (and_9_out, in_3, in_5);
  or or_5 (or_5_out, and_9_out, and_11_out);
  buf and_10 (and_10_out, in_10);  // AND_Gate
  and and_11 (and_11_out, not_1_out, out_13);
  D_Flip_Flop d_ff_5 (.D(or_5_out), .clk(clock_1_out), .Q(out_13), .reset(button_1_out));  // open: Qn, preset
  buf and_12 (and_12_out, not_2_out);  // AND_Gate
  or or_6 (or_6_out, and_10_out, and_12_out);
  and and_13 (and_13_out, in_4, in_5);
  D_Flip_Flop d_ff_6 (.D(or_6_out), .clk(clock_2_out), .reset(button_2_out));  // open: Q, Qn, preset
  and and_14 (and_14_out, not_1_out, out_11);
  or or_7 (or_7_out, and_13_out, and_14_out);
  buf and_15 (and_15_out, in_10);  // AND_Gate
  or or_8 (or_8_out, and_15_out, and_16_out);
  D_Flip_Flop d_ff_7 (.D(or_7_out), .clk(clock_1_out), .Q(out_11), .reset(button_1_out));  // open: Qn, preset
  buf and_16 (and_16_out, not_2_out);  // AND_Gate
  D_Flip_Flop d_ff_8 (.D(or_8_out), .clk(clock_2_out), .reset(button_2_out));  // open: Q, Qn, preset

  // Notes on the sheet:
  //   load
  //   reset
  //   load
  //   pulse
  //   pulse
  //   reset
  //   *1.* 4-bit shift register with parallel load: (PIPO)
  //   Data Input
  //   1 0 0 1
  //   1 0 1 0
  //   Truth - table: 
  //   1 0 0 1
  //   Data output
  //   1 0 1 0
endmodule
